# Fritzing sketch RPi W Protoboard (saved by Fritzing 0.9.1b)
breadboards: 1

parts:
  Raspberry_Pi_Zero1 = Raspberry Pi Zero  # not connected
  Grove1 = Grove OLED 128x96
  J1 = Raspberry Pi Header 40pin [form="♂ (male)" package=THT]
  Part1 = LSM303 Breakout Board - Tilt-Compensated Compass
  Exit = Momentary Switch [package=ksa_sealed_tac_switch]
  LOG = Momentary Switch [package=ksa_sealed_tac_switch]
  STDBY = Momentary Switch [package=ksa_sealed_tac_switch]
  LED1 = smd LED [color="Red (633nm)" package="0805 [SMD]"]
  Bump = smd LED [color="Blue (505nm)" package="0805 [SMD]"]
  R1 = Resistor [package="2512 [SMD]"]
  R2 = Resistor [tolerance=±5% resistance=220 package="0603 [SMD]"]

nets:
  GND: Grove1.GND, J1.GND, R2.Pin_0
  3V3: Grove1.VCC, J1.3v3, J1.3V3, LED1.anode
  N1: Grove1.SDA, Part1.SDA_M
  N2: Grove1.SCL, Part1.SCL_M
  N3: Exit.3, LOG.3, STDBY.3, R1.Pin_0
  N4: LED1.cathode, R2.Pin_1
  N5: Bump.cathode, R1.Pin_1

custom parts:
  Raspberry Pi Header 40pin: Raspberry Pi 40 pin header - for creating your own shields.
